// Logisim project circuit.circ as structural Verilog: 12 circuits, main circuit main
module main (
  input  [15:0] A,
  input  [15:0] B,
  input  SUB,
  output [15:0] Result_in_human_numbers
);

  wire SUB1_a_is_denormal, SUB1_a_is_infinity, SUB1_a_is_nan, SUB1_a_is_zero, SUB1_b_is_denormal,
       SUB1_b_is_infinity, SUB1_b_is_nan, SUB1_b_is_zero, SUB2_is_special, SUB3_eff_sign_b, SUB4_sign_a,
       SUB4_sign_b, SUB5_swap_flag, SUB7_eff_op, SUB8_result_negative, SUB9_result_is_inf,
       SUB9_result_is_zero, SUB10_final_sign;
  wire [4:0] SUB4_exp_a, SUB4_exp_b, SUB5_larger_exp, SUB5_shift_amount, SUB9_final_exp;
  wire [9:0] SUB9_norm_mantissa;
  wire [10:0] multiplexer_1_out, multiplexer_2_out, SUB4_mant_a, SUB4_mant_b, SUB6_shifted_mantissa;
  wire [11:0] SUB8_result_mantissa;
  wire [15:0] SUB2_special_result;

  // Probe on A
  // Probe on B
  // Probe on Result_in_human_numbers
  SpecialCaseDetector_SUB1 SUB1 (
    .A(A), .B(B), .SUB(SUB), .A_is_zero(SUB1_a_is_zero), .A_is_denormal(SUB1_a_is_denormal),
    .A_is_nan(SUB1_a_is_nan), .A_is_infinity(SUB1_a_is_infinity), .B_is_zero(SUB1_b_is_zero),
    .B_is_denormal(SUB1_b_is_denormal), .B_is_nan(SUB1_b_is_nan), .B_is_infinity(SUB1_b_is_infinity));
  SpecialCaseResultGen_SUB2 SUB2 (
    .A(A), .B(B), .SUB(SUB), .A_is_nan(SUB1_a_is_nan), .B_is_nan(SUB1_b_is_nan),
    .A_is_infinity(SUB1_a_is_infinity), .B_is_infinity(SUB1_b_is_infinity), .A_is_zero(SUB1_a_is_zero),
    .B_is_zero(SUB1_b_is_zero), .A_is_denormal(SUB1_a_is_denormal), .B_is_denormal(SUB1_b_is_denormal),
    .is_special(SUB2_is_special), .special_result(SUB2_special_result));  // open: out_12, out_13
  SignController_SUB3 SUB3 (.sign_B(SUB4_sign_b), .SUB(SUB), .eff_sign_B(SUB3_eff_sign_b));
  BitExtractor_SUB4 SUB4 (
    .A(A), .B(B), .A_is_denormal(SUB1_a_is_denormal), .B_is_denormal(SUB1_b_is_denormal),
    .sign_A(SUB4_sign_a), .exp_A(SUB4_exp_a), .mant_A(SUB4_mant_a), .sign_B(SUB4_sign_b), .exp_B(SUB4_exp_b),
    .mant_B(SUB4_mant_b));
  ExponentComparator_SUB5 SUB5 (
    .exp_A(SUB4_exp_a), .exp_B(SUB4_exp_b), .larger_exp(SUB5_larger_exp), .shift_amount(SUB5_shift_amount),
    .swap_flag(SUB5_swap_flag));
  EffOpDecider_SUB7 SUB7 (.sign_A(SUB4_sign_a), .eff_sign_B(SUB3_eff_sign_b), .eff_op(SUB7_eff_op));
  Multiplexer #(.width(11)) multiplexer_1 (
    .in0(SUB4_mant_b), .in1(SUB4_mant_a), .out(multiplexer_1_out), .sel(SUB5_swap_flag));
  Multiplexer #(.width(11)) multiplexer_2 (
    .in0(SUB4_mant_a), .in1(SUB4_mant_b), .out(multiplexer_2_out), .sel(SUB5_swap_flag));
  BarrelShifter_SUB6 SUB6 (
    .mantissa(multiplexer_1_out), .shift_amount(SUB5_shift_amount), .shifted_mantissa(SUB6_shifted_mantissa));
  MantissaAddSub_SUB8 SUB8 (
    .mant_A(multiplexer_2_out), .shifted_mant_B(SUB6_shifted_mantissa), .eff_op(SUB7_eff_op),
    .result_mantissa(SUB8_result_mantissa), .result_negative(SUB8_result_negative));
  Normaliser_SUB9 SUB9 (
    .result_mantissa(SUB8_result_mantissa), .larger_exp(SUB5_larger_exp), .norm_mantissa(SUB9_norm_mantissa),
    .final_exp(SUB9_final_exp), .result_is_inf(SUB9_result_is_inf), .result_is_zero(SUB9_result_is_zero));
  SignResolver_SUB10 SUB10 (
    .sign_A(SUB4_sign_a), .eff_sign_B(SUB3_eff_sign_b), .eff_op(SUB7_eff_op), .swap_flag(SUB5_swap_flag),
    .result_is_zero(SUB9_result_is_zero), .result_negative(SUB8_result_negative),
    .final_sign(SUB10_final_sign));
  OutputPacker_SUB11 SUB11 (
    .final_sign(SUB10_final_sign), .final_exp(SUB9_final_exp), .norm_mantissa(SUB9_norm_mantissa),
    .result_is_inf(SUB9_result_is_inf), .result_is_zero(SUB9_result_is_zero), .is_special(SUB2_is_special),
    .special_result(SUB2_special_result), .result(Result_in_human_numbers));  // open: result_is_denormal

  // Notes on the sheet:
  //   A in IEEE 754
  //   B in IEEE 754
  //   0 for ADDITION, 1 for SUBTRACT
  //   mant_swap_mux
  //   mant_larger_mux
endmodule

module SpecialCaseDetector_SUB1 (
  input  [15:0] A,
  input  [15:0] B,
  input  SUB,
  output A_is_zero,
  output A_is_denormal,
  output A_is_nan,
  output A_is_infinity,
  output B_is_zero,
  output B_is_denormal,
  output B_is_nan,
  output B_is_infinity
);

  wire exp_A_one_out, exp_A_zero_out, exp_B_one_out, exp_B_zero_out, mant_A_not_zero_out, mant_A_zero_out,
       mant_B_not_zero_out, mant_B_zero_out;

  nor mant_A_zero (mant_A_zero_out, A[0], A[1], A[2], A[3], A[4], A[5], A[6], A[7], A[8], A[9]);
  nor exp_A_zero (exp_A_zero_out, A[10], A[11], A[12], A[13], A[14]);
  and exp_A_one (exp_A_one_out, A[10], A[11], A[12], A[13], A[14]);
  nor mant_B_zero (mant_B_zero_out, B[0], B[1], B[2], B[3], B[4], B[5], B[6], B[7], B[8], B[9]);
  nor exp_B_zero (exp_B_zero_out, B[10], B[11], B[12], B[13], B[14]);
  and exp_B_one (exp_B_one_out, B[10], B[11], B[12], B[13], B[14]);
  not mant_A_not_zero (mant_A_not_zero_out, mant_A_zero_out);
  not mant_B_not_zero (mant_B_not_zero_out, mant_B_zero_out);
  and AND_A_zero (A_is_zero, exp_A_zero_out, mant_A_zero_out);
  and AND_A_denorm (A_is_denormal, exp_A_zero_out, mant_A_not_zero_out);
  and AND_A_nan (A_is_nan, exp_A_one_out, mant_A_not_zero_out);
  and AND_A_inf (A_is_infinity, exp_A_one_out, mant_A_zero_out);
  and AND_B_zero (B_is_zero, exp_B_zero_out, mant_B_zero_out);
  and AND_B_denorm (B_is_denormal, exp_B_zero_out, mant_B_not_zero_out);
  and AND_B_nan (B_is_nan, exp_B_one_out, mant_B_not_zero_out);
  and AND_B_inf (B_is_infinity, exp_B_one_out, mant_B_zero_out);
endmodule

module SpecialCaseResultGen_SUB2 (
  input  [15:0] A,
  input  [15:0] B,
  input  SUB,
  input  A_is_nan,
  input  B_is_nan,
  input  A_is_infinity,
  input  B_is_infinity,
  input  A_is_zero,
  input  B_is_zero,
  input  A_is_denormal,
  input  B_is_denormal,
  output [1:0] out_12,
  output [15:0] out_13,
  output is_special,
  output [15:0] special_result
);

  wire any_inf_out, any_nan_out, any_zero_out, inf_inf_nan_out, nan_case_out, signs_differ_out;
  wire [15:0] multiplexer_2_out;
  wire [15:15] eff_sign_B_out;

  xor eff_sign_B (eff_sign_B_out[15], SUB, B[15]);
  xor signs_differ (signs_differ_out, A[15], eff_sign_B_out[15]);
  or any_nan (any_nan_out, A_is_nan, B_is_nan);
  and inf_inf_nan (inf_inf_nan_out, A_is_infinity, signs_differ_out, B_is_infinity);
  or any_inf (any_inf_out, A_is_infinity, B_is_infinity);
  or any_zero (any_zero_out, A_is_zero, B_is_zero);
  or nan_case (nan_case_out, any_nan_out, inf_inf_nan_out);
  or is_special_gate (is_special, nan_case_out, any_inf_out, any_zero_out);
  Multiplexer #(.select(2), .width(16)) multiplexer_1 (
    .in0(A), .in1({eff_sign_B_out[15], B[14:0]}), .in2(multiplexer_2_out), .in3(16'h7e00),
    .out(special_result), .sel(out_12));
  Priority_Encoder #(.select(2)) priority_encoder_1 (
    .in0(B_is_zero), .in1(A_is_zero), .in2(any_inf_out), .in3(nan_case_out), .out(out_12));  // open: gs, en_out, en_in
  Multiplexer #(.width(16)) multiplexer_2 (
    .in0({eff_sign_B_out[15], B[14:0]}), .in1(A), .out(multiplexer_2_out), .sel(A_is_infinity));

  assign out_13 = 16'h7e00;

  // Notes on the sheet:
  //   join_eff_B
  //   NAN_const
  //   Zero_const
  //   priority_enc
  //   result mux
  //   Inf_mux
endmodule

module SignController_SUB3 (
  input  sign_B,
  input  SUB,
  output eff_sign_B
);

  xor sign_xor (eff_sign_B, sign_B, SUB);
endmodule

module BitExtractor_SUB4 (
  input  [15:0] A,
  input  [15:0] B,
  input  A_is_denormal,
  input  B_is_denormal,
  output sign_A,
  output [4:0] exp_A,
  output [10:0] mant_A,
  output sign_B,
  output [4:0] exp_B,
  output [10:0] mant_B
);

  Multiplexer multiplexer_1 (.in0(1'b1), .in1(1'b0), .out(mant_A[10]), .sel(A_is_denormal));
  Multiplexer multiplexer_2 (.in0(1'b1), .in1(1'b0), .out(mant_B[10]), .sel(B_is_denormal));

  assign exp_A = A[14:10];
  assign exp_B = B[14:10];
  assign mant_A[9:0] = A[9:0];
  assign mant_B[9:0] = B[9:0];
  assign sign_A = A[15];
  assign sign_B = B[15];

  // Notes on the sheet:
  //   hidden_one
  //   hidden_zero
  //   hidden_mux_A
  //   hidden_mux_B
  //   join_mant_A
  //   join_mant_B
endmodule

module ExponentComparator_SUB5 (
  input  [4:0] exp_A,
  input  [4:0] exp_B,
  output [4:0] larger_exp,
  output [4:0] shift_amount,
  output swap_flag
);

  wire [4:0] subtractor_1_out, subtractor_2_out;

  Subtractor #(.width(5)) subtractor_1 (.a(exp_A), .b(exp_B), .out(subtractor_1_out));  // open: bin, bout
  Comparator #(.mode("unsigned"), .width(5)) comparator_1 (.a(exp_A), .b(exp_B), .lt(swap_flag));  // open: gt, eq
  Subtractor #(.width(5)) subtractor_2 (.a(exp_B), .b(exp_A), .out(subtractor_2_out));  // open: bin, bout
  Multiplexer #(.width(5)) multiplexer_1 (.in0(exp_A), .in1(exp_B), .out(larger_exp), .sel(swap_flag));
  Multiplexer #(.width(5)) multiplexer_2 (
    .in0(subtractor_1_out), .in1(subtractor_2_out), .out(shift_amount), .sel(swap_flag));

  // Notes on the sheet:
  //   sub_A_minus_B
  //   exp_comparator
  //   sub_B_minus_A
  //   mux_shift_amt
  //   mux_larger_exp
endmodule

module BarrelShifter_SUB6 (
  input  [10:0] mantissa,
  input  [4:0] shift_amount,
  output [10:0] shifted_mantissa
);

  wire comparator_1_gt, force_zero_gate_out;
  wire [10:0] shifter_1_out;

  Shifter #(.shift("lr"), .width(11)) shifter_1 (.in(mantissa), .\dist (shift_amount[3:0]), .out(shifter_1_out));
  Comparator #(.mode("unsigned"), .width(4)) comparator_1 (
    .a(shift_amount[3:0]), .b(4'b1010), .gt(comparator_1_gt));  // open: eq, lt
  Multiplexer #(.width(11)) multiplexer_1 (
    .in0(shifter_1_out), .in1({11{1'b0}}), .out(shifted_mantissa), .sel(force_zero_gate_out));
  or force_zero_gate (force_zero_gate_out, shift_amount[4], comparator_1_gt);

  // Notes on the sheet:
  //   zero_11b
  //   right_shifter
  //   split_shift
  //   const_10
  //   output_mux
  //   shift_comparator
endmodule

module EffOpDecider_SUB7 (
  input  sign_A,
  input  eff_sign_B,
  output eff_op
);

  xnor op_xnor (eff_op, sign_A, eff_sign_B);
endmodule

module MantissaAddSub_SUB8 (
  input  [10:0] mant_A,
  input  [10:0] shifted_mant_B,
  input  eff_op,
  output [11:0] result_mantissa,
  output result_negative
);

  wire adder_1_cout, not_carry_out, not_eff_op_out;
  wire [10:0] adder_1_out, adder_2_out, invert_B_out, invert_sum_out, multiplexer_1_out;
  wire [11:0] bit_extender_1_out;
  wire [11:11] msb_gate_out;

  assign invert_B_out = ~shifted_mant_B;  // NOT_Gate invert_B, 11 bits wide
  Multiplexer #(.width(11)) multiplexer_1 (
    .in0(invert_B_out), .in1(shifted_mant_B), .out(multiplexer_1_out), .sel(eff_op));
  not not_eff_op (not_eff_op_out, eff_op);
  Adder #(.width(11)) adder_1 (
    .a(mant_A), .b(multiplexer_1_out), .out(adder_1_out), .cin(not_eff_op_out), .cout(adder_1_cout));
  and msb_gate (msb_gate_out[11], adder_1_cout, eff_op);
  not not_carry (not_carry_out, adder_1_cout);
  and neg_detector (result_negative, not_carry_out, not_eff_op_out);
  assign invert_sum_out = ~adder_1_out;  // NOT_Gate invert_sum, 11 bits wide
  Adder #(.width(11)) adder_2 (.a(invert_sum_out), .b({11{1'b0}}), .out(adder_2_out), .cin(1'b1));  // open: cout
  assign bit_extender_1_out = {{1{1'b0}}, adder_2_out};  // Bit_Extender bit_extender_1
  Multiplexer #(.width(12)) multiplexer_2 (
    .in0({msb_gate_out[11], adder_1_out}), .in1(bit_extender_1_out), .out(result_mantissa),
    .sel(result_negative));

  // Notes on the sheet:
  //   1:Add,0:Sub
  //   B_op_mux
  //   main_adder
  //   join_pos_12b
  //   const_1
  //   const_zero_11b
  //   neg_adder
  //   zero_extend
  //   final_mux
endmodule

module Normaliser_SUB9 (
  input  [11:0] result_mantissa,
  input  [4:0] larger_exp,
  output [9:0] norm_mantissa,
  output [4:0] final_exp,
  output result_is_inf,
  output result_is_zero
);

  wire [3:0] priority_encoder_1_out, subtractor_2_out;
  wire [4:0] adder_1_out, bit_extender_1_out, subtractor_1_out;
  wire [11:0] shifter_1_out, shifter_2_out;
  wire [11:10] multiplexer_2_out;

  Comparator #(.mode("unsigned"), .width(12)) comparator_1 (
    .a(result_mantissa), .b({12{1'b0}}), .eq(result_is_zero));  // open: gt, lt
  // Probe on priority_encoder_1_out
  Priority_Encoder #(.select(4)) priority_encoder_1 (
    .in0(result_mantissa[0]), .in1(result_mantissa[1]), .in2(result_mantissa[2]), .in3(result_mantissa[3]),
    .in4(result_mantissa[4]), .in5(result_mantissa[5]), .in6(result_mantissa[6]), .in7(result_mantissa[7]),
    .in8(result_mantissa[8]), .in9(result_mantissa[9]), .in10(result_mantissa[10]), .in11(1'b0), .in12(1'b0),
    .in13(1'b0), .in14(1'b0), .in15(1'b0), .out(priority_encoder_1_out));  // open: gs, en_out, en_in
  Subtractor #(.width(5)) subtractor_1 (
    .a(larger_exp), .b(bit_extender_1_out), .out(subtractor_1_out));  // open: bin, bout
  Adder #(.width(5)) adder_1 (.a(larger_exp), .b(5'b00001), .out(adder_1_out));  // open: cin, cout
  Subtractor #(.width(4)) subtractor_2 (
    .a(4'b1010), .b(priority_encoder_1_out), .out(subtractor_2_out));  // open: bin, bout
  Multiplexer #(.width(5)) multiplexer_1 (
    .in0(subtractor_1_out), .in1(adder_1_out), .out(final_exp), .sel(result_mantissa[11]));
  assign bit_extender_1_out = {{1{1'b0}}, subtractor_2_out};  // Bit_Extender bit_extender_1
  Comparator #(.mode("unsigned"), .width(5)) comparator_2 (
    .a(final_exp), .b(5'b11110), .gt(result_is_inf));  // open: eq, lt
  Shifter #(.width(12)) shifter_1 (.in(result_mantissa), .\dist (subtractor_2_out), .out(shifter_1_out));
  Shifter #(.shift("lr"), .width(12)) shifter_2 (.in(result_mantissa), .\dist (4'b0001), .out(shifter_2_out));
  Multiplexer #(.width(12)) multiplexer_2 (
    .in0(shifter_1_out), .in1(shifter_2_out), .out({multiplexer_2_out, norm_mantissa}),
    .sel(result_mantissa[11]));

  // Notes on the sheet:
  //   const0_12b
  //   zero_check
  //   split_top
  //   const0_1b
  //   split_11bits
  //   const1_5b
  //   lzc_encoder
  //   exp_dec
  //   exp_inc
  //   const_10
  //   exp_mux
  //   shift_calc
  //   const_30
  //   extend_shift
  //   overflow_check
  //   const1_4b
  //   left_shifter
  //   right_shifter
  //   shift_mux
  //   strip_hidden
endmodule

module SignResolver_SUB10 (
  input  sign_A,
  input  eff_sign_B,
  input  eff_op,
  input  swap_flag,
  input  result_is_zero,
  input  result_negative,
  output final_sign
);

  wire multiplexer_1_out, not_eff_op_out, not_zero_out, or_gate_out, use_B_sign_gate_out;

  or or_gate (or_gate_out, swap_flag, result_negative);
  not not_eff_op (not_eff_op_out, eff_op);
  and use_B_sign_gate (use_B_sign_gate_out, or_gate_out, not_eff_op_out);
  Multiplexer multiplexer_1 (.in0(sign_A), .in1(eff_sign_B), .out(multiplexer_1_out), .sel(use_B_sign_gate_out));
  not not_zero (not_zero_out, result_is_zero);
  and final_and (final_sign, multiplexer_1_out, not_zero_out);

  // Notes on the sheet:
  //   sign_mux
endmodule

module OutputPacker_SUB11 (
  input  final_sign,
  input  [4:0] final_exp,
  input  [9:0] norm_mantissa,
  input  result_is_inf,
  input  result_is_zero,
  input  is_special,
  input  [15:0] special_result,
  input  result_is_denormal,
  output [15:0] result
);

  wire [15:0] multiplexer_1_out, multiplexer_2_out;

  Multiplexer #(.width(16)) multiplexer_1 (
    .in0({final_sign, final_exp, norm_mantissa}), .in1({final_sign, 15'h7c00}), .out(multiplexer_1_out),
    .sel(result_is_inf));
  Multiplexer #(.width(16)) multiplexer_2 (
    .in0(multiplexer_1_out), .in1({16{1'b0}}), .out(multiplexer_2_out), .sel(result_is_zero));
  Multiplexer #(.width(16)) multiplexer_3 (
    .in0(multiplexer_2_out), .in1(special_result), .out(result), .sel(is_special));

  // Notes on the sheet:
  //   const_inf_exp
  //   const_zero_mant
  //   const_zero_16b
  //   join_normal
  //   join_inf
  //   mux_inf
  //   mux_zero
  //   final_mux
endmodule
